// Logisim project Milestone1.circ as structural Verilog
module OneBitAdder (
  input  A,
  input  B,
  input  C_in,
  output S,
  output C_out
);

  wire and_1_out, and_2_out, and_3_out, and_4_out, and_5_out, and_6_out, and_7_out, not_1_out, not_2_out,
       not_3_out;

  not not_1 (not_1_out, A);
  not not_2 (not_2_out, B);
  not not_3 (not_3_out, C_in);
  and and_1 (and_1_out, not_1_out, not_2_out, C_in);
  and and_2 (and_2_out, not_1_out, B, not_3_out);
  and and_3 (and_3_out, A, not_2_out, not_3_out);
  and and_4 (and_4_out, A, B, C_in);
  and and_5 (and_5_out, B, C_in);
  and and_6 (and_6_out, A, C_in);
  and and_7 (and_7_out, A, B);
  or or_1 (S, and_1_out, and_2_out, and_3_out, and_4_out);
  or or_2 (C_out, and_5_out, and_6_out, and_7_out);
endmodule

module ALU_Ctrl (
  input  I30,
  input  I14,
  input  I13,
  input  I12,
  input  I6,
  input  I5,
  input  I4,
  output ALU_Ctrl3,
  output ALU_Ctrl2,
  output ALU_Ctrl1,
  output ALU_Ctrl0,
  output ALU_Src
);

  wire and_2_out, not_1_out, not_2_out, not_3_out, not_4_out, not_5_out;

  not not_1 (not_1_out, I14);
  not not_2 (not_2_out, I13);
  not not_3 (not_3_out, I12);
  not not_4 (not_4_out, I5);
  not not_5 (not_5_out, I4);
  and and_1 (ALU_Ctrl2, I30, not_2_out, I5);
  or or_1 (ALU_Ctrl1, not_2_out, not_5_out);
  and and_2 (and_2_out, I13, not_3_out);
  or or_2 (ALU_Src, not_4_out, not_5_out);
  or or_3 (ALU_Ctrl0, not_1_out, and_2_out);

  assign ALU_Ctrl3 = 1'b0;
endmodule

module One_Bit_ALU (
  input  [3:0] ALU_Ctrl_in,
  input  A,
  input  B,
  input  C_in,
  output R,
  output C_out
);

  wire and_1_out, multiplexer_1_out, not_1_out, onebitadder_1_s, or_1_out, xor_1_out;

  not not_1 (not_1_out, B);
  Multiplexer #(.enable("false")) multiplexer_1 (
    .in0(B), .in1(not_1_out), .out(multiplexer_1_out), .sel(ALU_Ctrl_in[2]));
  and and_1 (and_1_out, A, multiplexer_1_out);
  or or_1 (or_1_out, A, multiplexer_1_out);
  xor xor_1 (xor_1_out, A, multiplexer_1_out);
  OneBitAdder onebitadder_1 (.A(A), .B(multiplexer_1_out), .C_in(C_in), .S(onebitadder_1_s), .C_out(C_out));
  Multiplexer #(.enable("false"), .select(2)) multiplexer_2 (
    .in0(and_1_out), .in1(or_1_out), .in2(xor_1_out), .in3(onebitadder_1_s), .out(R), .sel(ALU_Ctrl_in[1:0]));
endmodule

module Four_Bit_ALU (
  input  [3:0] ALU_Ctrl,
  input  [3:0] A,
  input  C_in,
  input  [3:0] B,
  output [3:0] R,
  output C_out
);

  wire one_bit_alu_1_c_out, one_bit_alu_2_c_out, one_bit_alu_3_c_out;

  One_Bit_ALU one_bit_alu_1 (
    .ALU_Ctrl_in(ALU_Ctrl), .A(A[0]), .B(B[0]), .C_in(C_in), .R(R[0]), .C_out(one_bit_alu_1_c_out));
  One_Bit_ALU one_bit_alu_2 (
    .ALU_Ctrl_in(ALU_Ctrl), .A(A[1]), .B(B[1]), .C_in(one_bit_alu_1_c_out), .R(R[1]),
    .C_out(one_bit_alu_2_c_out));
  One_Bit_ALU one_bit_alu_3 (
    .ALU_Ctrl_in(ALU_Ctrl), .A(A[2]), .B(B[2]), .C_in(one_bit_alu_2_c_out), .R(R[2]),
    .C_out(one_bit_alu_3_c_out));
  One_Bit_ALU one_bit_alu_4 (
    .ALU_Ctrl_in(ALU_Ctrl), .A(A[3]), .B(B[3]), .C_in(one_bit_alu_3_c_out), .R(R[3]), .C_out(C_out));
endmodule

module ThirtyTwo_Bit_ALU (
  input  C_in,
  input  [3:0] ALU_Ctrl,
  input  [31:0] A,
  input  [31:0] B,
  output [31:0] R,
  output C_out
);

  wire four_bit_alu_1_c_out, four_bit_alu_2_c_out, four_bit_alu_3_c_out, four_bit_alu_4_c_out,
       four_bit_alu_5_c_out, four_bit_alu_6_c_out, four_bit_alu_7_c_out;

  Four_Bit_ALU four_bit_alu_1 (
    .ALU_Ctrl(ALU_Ctrl), .A(A[3:0]), .C_in(C_in), .B(B[3:0]), .R(R[3:0]), .C_out(four_bit_alu_1_c_out));
  Four_Bit_ALU four_bit_alu_2 (
    .ALU_Ctrl(ALU_Ctrl), .A(A[7:4]), .C_in(four_bit_alu_1_c_out), .B(B[7:4]), .R(R[7:4]),
    .C_out(four_bit_alu_2_c_out));
  Four_Bit_ALU four_bit_alu_3 (
    .ALU_Ctrl(ALU_Ctrl), .A(A[11:8]), .C_in(four_bit_alu_2_c_out), .B(B[11:8]), .R(R[11:8]),
    .C_out(four_bit_alu_3_c_out));
  Four_Bit_ALU four_bit_alu_4 (
    .ALU_Ctrl(ALU_Ctrl), .A(A[15:12]), .C_in(four_bit_alu_3_c_out), .B(B[15:12]), .R(R[15:12]),
    .C_out(four_bit_alu_4_c_out));
  Four_Bit_ALU four_bit_alu_5 (
    .ALU_Ctrl(ALU_Ctrl), .A(A[19:16]), .C_in(four_bit_alu_4_c_out), .B(B[19:16]), .R(R[19:16]),
    .C_out(four_bit_alu_5_c_out));
  Four_Bit_ALU four_bit_alu_6 (
    .ALU_Ctrl(ALU_Ctrl), .A(A[23:20]), .C_in(four_bit_alu_5_c_out), .B(B[23:20]), .R(R[23:20]),
    .C_out(four_bit_alu_6_c_out));
  Four_Bit_ALU four_bit_alu_7 (
    .ALU_Ctrl(ALU_Ctrl), .A(A[27:24]), .C_in(four_bit_alu_6_c_out), .B(B[27:24]), .R(R[27:24]),
    .C_out(four_bit_alu_7_c_out));
  Four_Bit_ALU four_bit_alu_8 (
    .ALU_Ctrl(ALU_Ctrl), .A(A[31:28]), .C_in(four_bit_alu_7_c_out), .B(B[31:28]), .R(R[31:28]), .C_out(C_out));
endmodule
